// Digital circuit 16bits_alu.dig as structural Verilog
module _16bits_alu (
  input  [15:0] A,
  input  [15:0] B,
  input  [1:0] Sel,
  output [15:0] S,
  output C_out,
  output ZF
);

  wire Add_c_o, Sub_c_o;
  wire [15:0] Add_s, and_1_out, or_1_out, Sub_s;

  Add #(.Bits(16)) Add (.a(A), .b(B), .c_i(1'b0), .s(Add_s), .c_o(Add_c_o));
  Sub #(.Bits(16)) Sub (.a(A), .b(B), .c_i(1'b0), .s(Sub_s), .c_o(Sub_c_o));
  assign and_1_out = A & B;  // And and_1, 16 bits wide
  assign or_1_out = A | B;  // Or or_1, 16 bits wide
  Multiplexer multiplexer_1 (.sel(Sel[0]), .in_0(Add_c_o), .in_1(Sub_c_o), .out(C_out));
  Multiplexer #(.Selector_Bits(2), .Bits(16)) multiplexer_2 (
    .sel(Sel), .in_0(Add_s), .in_1(Sub_s), .in_2(and_1_out), .in_3(or_1_out), .out(S));
  Comparator #(.Bits(16)) comparator_1 (.a(A), .b(B), .eq(ZF));  // open: gt, lt
endmodule
