// Digital circuit 16bits_caculator.dig as structural Verilog
module _16bits_caculator (
  input  [15:0] A,
  input  [1:0] Sel,
  input  EN,
  output [15:0] S
);

  wire button_1_out;
  wire [15:0] _16bits_alu_1_s;

  _16bits_alu _16bits_alu_1 (.A(S), .B(A), .Sel(Sel), .S(_16bits_alu_1_s));  // open: C_out, ZF
  Button button_1 (.out(button_1_out));
  Register #(.Bits(16)) register_1 (.D(_16bits_alu_1_s), .C(button_1_out), .en(EN), .Q(S));
endmodule
