// Digital circuit 1bit_mux.dig as structural Verilog
module _1bit_mux (
  input  S_1,
  input  S_2,
  input  Sel,
  output S
);

  // RelayDT relaydt_1: pin names not known; wires that end beside it: Sel, S_2, S_1, 1'b0, S
endmodule
