// Digital circuit 2bit_adder.dig as structural Verilog
module _2bit_adder (
  input  B_0,
  input  B_1,
  input  A_0,
  input  A_1,
  input  C_in,
  output C_out,
  output _1,
  output _0
);

  wire full_adder_henry_1_c_out;

  full_adder_henry full_adder_henry_1 (.A(A_0), .B(B_0), .C_in(C_in), .S(_0), .C_out(full_adder_henry_1_c_out));
  full_adder_henry full_adder_henry_2 (.A(A_1), .B(B_1), .C_in(full_adder_henry_1_c_out), .S(_1), .C_out(C_out));
endmodule
