// Digital circuit 2bit_counter.dig as structural Verilog
module _2bit_counter (
  input  C,
  input  en,
  output [3:0] out,
  output ovf
);

  wire [3:0] add_1_s;

  Register #(.Bits(4)) register_1 (.D(add_1_s), .C(C), .en(en), .Q(out));
  Add #(.Bits(4)) add_1 (.a(out), .b(4'b0001), .c_i(1'b0), .s(add_1_s), .c_o(ovf));
endmodule
