// Digital circuit 38_decoder.dig as structural Verilog
module _38_decoder (
  input  C,
  input  B,
  input  A,
  output S0,
  output S1,
  output S2,
  output S3,
  output S4,
  output S5,
  output S6,
  output S7
);

  wire not_1_out, not_2_out, not_3_out;

  not not_1 (not_1_out, A);
  not not_2 (not_2_out, B);
  not not_3 (not_3_out, C);
  and and_1 (S0, not_1_out, not_2_out, not_3_out);
  and and_2 (S1, not_1_out, not_2_out, C);
  and and_3 (S2, not_1_out, B, not_3_out);
  and and_4 (S3, not_1_out, B, C);
  and and_5 (S4, A, not_2_out, not_3_out);
  and and_6 (S5, A, not_2_out, C);
  and and_7 (S6, A, B, not_3_out);
  and and_8 (S7, A, B, C);
endmodule
