// Digital circuit 4bit_mux.dig as structural Verilog
module _4bit_mux (
  input  S_1,
  input  S_2,
  input  S_3,
  input  S_4,
  input  [1:0] Sel,
  output S
);

  wire _1bit_mux_1_s, _1bit_mux_2_s;

  _1bit_mux _1bit_mux_1 (.S_1(S_1), .S_2(S_2), .Sel(Sel[0]), .S(_1bit_mux_1_s));
  _1bit_mux _1bit_mux_2 (.S_1(S_3), .S_2(S_4), .Sel(Sel[0]), .S(_1bit_mux_2_s));
  _1bit_mux _1bit_mux_3 (.S_1(_1bit_mux_1_s), .S_2(_1bit_mux_2_s), .Sel(Sel[1]), .S(S));
endmodule
