// Digital circuit 4bit_reg.dig as structural Verilog
module _4bit_reg (
  input  D_3,
  input  D_2,
  input  D_1,
  input  D_0,
  input  en,
  input  C,
  output Q_3,
  output Q_2,
  output Q_1,
  output Q_0
);

  wire and_1_out;

  and and_1 (and_1_out, C, en);
  d_flip_flop d_flip_flop_1 (.D(D_0), .EN(and_1_out), .Q(Q_0));  // open: Q_2
  d_flip_flop d_flip_flop_2 (.D(D_1), .EN(and_1_out), .Q(Q_1));  // open: Q_2
  d_flip_flop d_flip_flop_3 (.D(D_2), .EN(and_1_out), .Q(Q_2));  // open: Q_2
  d_flip_flop d_flip_flop_4 (.D(D_3), .EN(and_1_out), .Q(Q_3));  // open: Q_2
endmodule
