// Digital circuit Comparator.dig as structural Verilog
module Comparator (
  input  A,
  input  B,
  output ZF
);

  wire and_1_out, and_2_out, not_1_out, not_2_out;

  not not_1 (not_1_out, A);
  not not_2 (not_2_out, B);
  and and_1 (and_1_out, not_2_out, not_1_out);
  and and_2 (and_2_out, B, A);
  or or_1 (ZF, and_1_out, and_2_out);
endmodule
