// Digital circuit and_gate.dig as structural Verilog
module and_gate (
  input  A,
  input  B,
  output C
);

  wire relay_1_p4;

  // Relay relay_1: pin names not known; wires that end beside it: A, 1'b1, 1'b0, relay_1_p4
  // Relay relay_2: pin names not known; wires that end beside it: B, relay_1_p4, 1'b0, C
endmodule
