// Digital circuit combine_cpu.dig as structural Verilog
module combine_cpu (
  input  C,
  input  ld,
  input  en,
  input  str,
  input  [15:0] D_in,
  output [15:0] A,
  output C_out,
  output ZF
);

  wire [1:0] _2bit_counter_1_p3, eepromdualport_2_d;
  wire [15:0] _16bits_alu_1_s, eepromdualport_1_d;

  // _2bit_counter _2bit_counter_1: pin names not known; wires that end beside it: C, en, _2bit_counter_1_p3
  Register #(.Bits(16)) register_1 (.D(_16bits_alu_1_s), .C(C), .en(en), .Q(A));
  EEPROMDualPort #(.Bits(16)) eepromdualport_1 (
    .A(_2bit_counter_1_p3), .Din(D_in), .str(str), .C(C), .ld(ld), .D(eepromdualport_1_d));
  EEPROMDualPort #(.Bits(2)) eepromdualport_2 (
    .A(_2bit_counter_1_p3), .Din(2'b00), .str(1'b0), .C(C), .ld(ld), .D(eepromdualport_2_d));
  _16bits_alu _16bits_alu_1 (
    .A(A), .B(eepromdualport_1_d), .Sel(eepromdualport_2_d), .S(_16bits_alu_1_s), .C_out(C_out), .ZF(ZF));

  // Notes on the sheet:
  //   contents of eepromdualport_1 (hex, n*v repeats v):
  //   a,14,1e,28
  //   contents of eepromdualport_2 (hex, n*v repeats v):
  //   0,0,0,1
endmodule
