// Digital circuit d_flip_flop.dig as structural Verilog
module d_flip_flop (
  input  D,
  input  EN,
  output Q,
  output Q_2
);

  wire d_latch_1_q, not_1_out;

  not not_1 (not_1_out, EN);
  d_latch d_latch_1 (.D(D), .EN(not_1_out), .Q(d_latch_1_q));  // open: Q_2
  d_latch d_latch_2 (.D(d_latch_1_q), .EN(EN), .Q(Q), .Q_2(Q_2));
endmodule
