// Digital circuit d_latch.dig as structural Verilog
module d_latch (
  input  D,
  input  EN,
  output Q,
  output Q_2
);

  wire nand_1_out, nand_2_out, not_1_out;

  not not_1 (not_1_out, D);
  nand nand_1 (nand_1_out, D, EN);
  nand nand_2 (nand_2_out, EN, not_1_out);
  rs_latch rs_latch_1 (.S(nand_1_out), .R(nand_2_out), .Q(Q), .Q_2(Q_2));
endmodule
