// Digital circuit eeprom.dig as structural Verilog
module eeprom (
  input  [2:0] A,
  input  [15:0] D_in,
  input  Str,
  input  ld,
  input  C,
  output [15:0] D
);

  wire _38_decoder_1_s0, _38_decoder_1_s1, _38_decoder_1_s2, _38_decoder_1_s3, _38_decoder_1_s4,
       _38_decoder_1_s5, _38_decoder_1_s6, _38_decoder_1_s7, and_1_out;
  wire [15:0] multiplexer_1_out, register_1_q, register_2_q, register_3_q, register_4_q, register_5_q,
       register_6_q, register_7_q, register_8_q;

  and and_1 (and_1_out, C, Str);
  _38_decoder _38_decoder_1 (
    .C(A[0]), .B(A[1]), .A(A[2]), .S0(_38_decoder_1_s0), .S1(_38_decoder_1_s1), .S2(_38_decoder_1_s2),
    .S3(_38_decoder_1_s3), .S4(_38_decoder_1_s4), .S5(_38_decoder_1_s5), .S6(_38_decoder_1_s6),
    .S7(_38_decoder_1_s7));
  Register #(.Bits(16)) register_1 (.D(D_in), .C(and_1_out), .en(_38_decoder_1_s0), .Q(register_1_q));
  Register #(.Bits(16)) register_2 (.D(D_in), .C(and_1_out), .en(_38_decoder_1_s1), .Q(register_2_q));
  Register #(.Bits(16)) register_3 (.D(D_in), .C(and_1_out), .en(_38_decoder_1_s2), .Q(register_3_q));
  Register #(.Bits(16)) register_4 (.D(D_in), .C(and_1_out), .en(_38_decoder_1_s3), .Q(register_4_q));
  Register #(.Bits(16)) register_5 (.D(D_in), .C(and_1_out), .en(_38_decoder_1_s4), .Q(register_5_q));
  Register #(.Bits(16)) register_6 (.D(D_in), .C(and_1_out), .en(_38_decoder_1_s5), .Q(register_6_q));
  Register #(.Bits(16)) register_7 (.D(D_in), .C(and_1_out), .en(_38_decoder_1_s6), .Q(register_7_q));
  Register #(.Bits(16)) register_8 (.D(D_in), .C(and_1_out), .en(_38_decoder_1_s7), .Q(register_8_q));
  Multiplexer #(.Bits(16), .Selector_Bits(3)) multiplexer_1 (
    .sel(A), .in_0(register_1_q), .in_1(register_2_q), .in_2(register_3_q), .in_3(register_4_q),
    .in_4(register_5_q), .in_5(register_6_q), .in_6(register_7_q), .in_7(register_8_q),
    .out(multiplexer_1_out));
  assign D = ld ? multiplexer_1_out : 16'bz;  // Driver driver_1
endmodule
