// Digital circuit full_adder.dig as structural Verilog
module full_adder (
  input  A,
  input  B,
  input  C_in,
  output S,
  output C_out
);

  wire half_adder_1_c, half_adder_1_s, half_adder_2_c;

  half_adder half_adder_1 (.A(B), .B(A), .S(half_adder_1_s), .C(half_adder_1_c));
  half_adder half_adder_2 (.A(C_in), .B(half_adder_1_s), .S(S), .C(half_adder_2_c));
  or or_1 (C_out, half_adder_2_c, half_adder_1_c);
endmodule
