// Digital circuit not_gate.dig as structural Verilog
module not_gate (
  input  A,
  input  B,
  input  in_5,
  input  in_6,
  output C,
  output out_4
);

  wire relay_1_p4;

  // Relay relay_1: pin names not known; wires that end beside it: A, 1'b1, 1'b0, relay_1_p4
  and and_1 (out_4, in_5, in_6);
  // Relay relay_2: pin names not known; wires that end beside it: B, relay_1_p4, 1'b0, C
endmodule
