// Digital circuit or_gate.dig as structural Verilog
module or_gate (
  input  A,
  input  B,
  output C
);

  // Relay relay_1: pin names not known; wires that end beside it: 1'b1, C
  // Relay relay_2: pin names not known; wires that end beside it: A, 1'b1, B, 1'b0, C, 1'b0
endmodule
